# Fritzing sketch ADSR_SW+AMP (saved by Fritzing 0.9.4)
breadboards: 3

parts:
  R1 = Resistor [tolerance=±5% resistance=22k package=THT]
  R2 = Rotary Potentiometer (Small) [maximum_resistance=100kΩ package=THT]
  Q1 = PNP-Transistor [package="TO92 [THT]"]
  R3 = Rotary Potentiometer (Small) [maximum_resistance=100kΩ package=THT]
  C1 = Electrolytic Capacitor [capacitance=1µF package="100 mil [THT, electrolytic]"]
  R4 = Rotary Potentiometer (Small) [maximum_resistance=100kΩ package=THT]
  R5 = Rotary Potentiometer (Small) [maximum_resistance=100kΩ package=THT]
  パーツ1 = Arduino Uno (Rev3)
  R6 = Resistor [tolerance=±5% resistance=150 package=THT]
  R7 = Resistor [tolerance=±5% resistance=150 package=THT]
  IC1 = Dual Op-Amp [package=dip08]
  C2 = Ceramic Capacitor [capacitance=100nF package="100 mil [THT, multilayer]"]
  C3 = Ceramic Capacitor [capacitance=100nF package="100 mil [THT, multilayer]"]
  R8 = Resistor [tolerance=±5% resistance=100k package=THT]
  R9 = Resistor [tolerance=±5% resistance=100k package=THT]
  R10 = Resistor [tolerance=±5% resistance=100k package=THT]
  R11 = Resistor [tolerance=±5% resistance=100k package=THT]
  R12 = Resistor [tolerance=±5% resistance=1k package=THT]
  R13 = Resistor [tolerance=±5% resistance=1k package=THT]
  C4 = Electrolytic Capacitor [capacitance=1µF package="100 mil [THT, electrolytic]"]
  C5 = Electrolytic Capacitor [capacitance=1µF package="100 mil [THT, electrolytic]"]
  R14 = Rotary Potentiometer (Small) [maximum_resistance=100kΩ package=THT]
  R15 = Resistor [tolerance=±5% resistance=1k package=THT]
  C6 = Ceramic Capacitor [capacitance=100nF package="100 mil [THT, multilayer]"]
  S1 = Pushbutton [package="[THT]"]
  R16 = Resistor [tolerance=±5% resistance=100k package=THT]

nets:
  N1: R1.Pin_0, パーツ1.5V, R14.wiper, R14.leg2, R15.Pin_0, S1.Pin_1, S1.Pin_2
  N2: R1.Pin_1, R2.leg2
  N3: R2.leg1, パーツ1.D6_PWM
  N4: R2.wiper, Q1.C
  N5: Q1.E, R3.wiper, R3.leg2
  N6: Q1.B, C1.-, パーツ1.GND, IC1.A_+IN, C2.1, R9.Pin_0, C4.-, C5.+, R14.leg1, C6.0, R16.Pin_0
  N7: R3.leg1, C1.+, R4.wiper, R4.leg2, R5.wiper, R5.leg2, パーツ1.A0, IC1.B_+IN
  N8: R4.leg1, R6.Pin_0
  N9: R5.leg1, R7.Pin_0
  N10: パーツ1.A1, R15.Pin_1, C6.1
  N11: パーツ1.D3_PWM, S1.Pin_3, S1.Pin_4, R16.Pin_1
  N12: パーツ1.D5_PWM, R6.Pin_1
  N13: パーツ1.D7, R7.Pin_1
  N14: IC1.A_OUT, R10.Pin_0, R12.Pin_1
  N15: IC1.A_-IN, R10.Pin_1, R11.Pin_0
  N16: IC1.A_V-, C3.0, C5.-
  N17: IC1.B_-IN, R8.Pin_1, R9.Pin_1
  N18: IC1.B_OUT, R8.Pin_0, R11.Pin_1, R13.Pin_1
  N19: IC1.A_V+, C2.0, C4.+

notes:
  Rsustain
  50k/A
  Rdecay
  50k/A
  Rattack
  50k/A
  Rrelease
  50k/A
  GND
  +5V
  ADSR
  OUT
  INV
  -12V
  GND
  GND
  +12V
  DelayTime
  50k/B
  Gate SW
  Delayed Gate
