# Fritzing sketch ADSR_SW (saved by Fritzing 0.9.4)
breadboards: 1

parts:
  R1 = Resistor [tolerance=±5% resistance=22k package=THT]
  R2 = Rotary Potentiometer (Small) [maximum_resistance=100kΩ package=THT]
  Q1 = PNP-Transistor [package="TO92 [THT]"]
  R3 = Rotary Potentiometer (Small) [maximum_resistance=100kΩ package=THT]
  C1 = Electrolytic Capacitor [capacitance=1µF package="100 mil [THT, electrolytic]"]
  R4 = Rotary Potentiometer (Small) [maximum_resistance=100kΩ package=THT]
  R5 = Rotary Potentiometer (Small) [maximum_resistance=100kΩ package=THT]
  パーツ1 = Arduino Uno (Rev3)
  R6 = Resistor [tolerance=±5% resistance=150 package=THT]
  R7 = Resistor [tolerance=±5% resistance=150 package=THT]

nets:
  N1: R1.Pin_0, パーツ1.5V
  N2: R1.Pin_1, R2.leg2
  N3: R2.leg1, パーツ1.D6_PWM
  N4: R2.wiper, Q1.C
  N5: Q1.E, R3.wiper, R3.leg2
  N6: Q1.B, C1.-, パーツ1.GND
  N7: R3.leg1, C1.+, R4.wiper, R4.leg2, R5.wiper, R5.leg2
  N8: R4.leg1, R6.Pin_0
  N9: R5.leg1, R7.Pin_0
  N10: パーツ1.D5_PWM, R6.Pin_1
  N11: パーツ1.D7, R7.Pin_1

notes:
  Rsustain
  50k/A
  Rdecay
  50k/A
  Rattack
  50k/A
  Rrelease
  50k/A
  GND
  +5V
  ADSR_OUT
