# Fritzing sketch ADSR_SW_Comparator_Hys_NonInv_Test (saved by Fritzing 0.9.4)
breadboards: 1

parts:
  R1 = Resistor [tolerance=±5% resistance=22k package=THT]
  R2 = Rotary Potentiometer (Small) [maximum_resistance=100kΩ package=THT]
  Q1 = PNP-Transistor [package="TO92 [THT]"]
  R3 = Rotary Potentiometer (Small) [maximum_resistance=100kΩ package=THT]
  C1 = Electrolytic Capacitor [capacitance=1µF package="100 mil [THT, electrolytic]"]
  R4 = Rotary Potentiometer (Small) [maximum_resistance=100kΩ package=THT]
  R5 = Rotary Potentiometer (Small) [maximum_resistance=100kΩ package=THT]
  パーツ1 = Arduino Uno (Rev3)
  R6 = Resistor [tolerance=±5% resistance=150 package=THT]
  R7 = Resistor [tolerance=±5% resistance=150 package=THT]
  IC2 = Dual Op-Amp [package=dip08]
  C7 = Ceramic Capacitor [capacitance=100nF package="100 mil [THT, multilayer]"]
  R17 = Resistor [tolerance=±5% resistance=12k package=THT]
  R18 = Resistor [tolerance=±5% resistance=22k package=THT]
  R19 = Resistor [tolerance=±5% resistance=1k package=THT]
  LED1 = LED - 3mm [color="Green (570nm)" package="3 mm [THT]"]
  C8 = Electrolytic Capacitor [capacitance=1µF package="100 mil [THT, electrolytic]"]
  R20 = Resistor [tolerance=±5% resistance=100k package=THT]
  R21 = Resistor [tolerance=±5% resistance=4.7k package=THT]

nets:
  N1: R1.Pin_0, IC2.A_V+, C7.0, R17.Pin_0, C8.+
  N2: R1.Pin_1, R2.leg2
  N3: R2.leg1, パーツ1.D6_PWM
  N4: R2.wiper, Q1.C
  N5: Q1.E, R3.wiper, R3.leg2
  N6: Q1.B, C1.-, IC2.A_V-, C7.1, R18.Pin_0, LED1.cathode, C8.-
  N7: R3.leg1, C1.+, R4.wiper, R4.leg2, R5.wiper, R5.leg2, IC2.A_+IN, R21.Pin_0
  N8: R4.leg1, R6.Pin_0
  N9: R5.leg1, R7.Pin_0
  N10: パーツ1.D2, IC2.B_OUT, R20.Pin_1
  N11: パーツ1.D5_PWM, R6.Pin_1
  N12: パーツ1.D7, R7.Pin_1
  N13: IC2.A_OUT, IC2.A_-IN, R19.Pin_1
  N14: IC2.B_+IN, R20.Pin_0, R21.Pin_1
  N15: IC2.B_-IN, R17.Pin_1, R18.Pin_1
  N16: R19.Pin_0, LED1.anode

notes:
  Rsustain
  50k/A
  Rdecay
  50k/A
  Rattack
  50k/A
  Rrelease
  50k/A
  GND
  +5V
  ADSR
