# Fritzing sketch ADSR_SW_Test (saved by Fritzing 0.9.4)
breadboards: 1

parts:
  パーツ1 = Arduino Uno (Rev3)
  R1 = Resistor [tolerance=±5% resistance=1k package=THT]
  R2 = Resistor [tolerance=±5% resistance=1k package=THT]
  R3 = Resistor [tolerance=±5% resistance=1k package=THT]

nets:
  N1: パーツ1.D5_PWM, R3.Pin_1
  N2: パーツ1.D6_PWM, R2.Pin_1
  N3: パーツ1.D7, R1.Pin_1
  N4: パーツ1.5V, R3.Pin_0
  N5: パーツ1.GND, R1.Pin_0, R2.Pin_0
