# Fritzing sketch Gate_In_Limitter+Delay_Time_Test (saved by Fritzing 0.9.4)
breadboards: 1

parts:
  R2 = Resistor [tolerance=±5% resistance=4.7k package=THT]
  D1 = Rectifier Diode [part_number=1N4001 package="300 mil [THT]"]
  D2 = Rectifier Diode [part_number=1N4001 package="300 mil [THT]"]
  D3 = Rectifier Diode [part_number=1N4001 package="300 mil [THT]"]
  R3 = Resistor [tolerance=±5% resistance=100k package=THT]
  S1 = Pushbutton [package="[THT]"]
  R4 = Resistor [tolerance=±5% resistance=100k package=THT]
  R5 = Resistor [tolerance=±5% resistance=1k package=THT]
  C1 = Ceramic Capacitor [capacitance=100nF package="100 mil [THT, multilayer]"]
  R6 = Rotary Potentiometer (Small) [maximum_resistance=100kΩ package=THT]
  パーツ1 = Arduino Uno (Rev3)
  C2 = Electrolytic Capacitor [capacitance=1µF package="100 mil [THT, electrolytic]"]

nets:
  N1: R2.Pin_0, R4.Pin_1
  N2: R2.Pin_1, D1.anode, D2.cathode, D3.anode
  N3: D1.cathode, S1.Pin_1, S1.Pin_2, R6.leg2, パーツ1.5V, C2.+
  N4: D2.anode, R3.Pin_0, R4.Pin_0, C1.0, R6.leg1, パーツ1.GND, C2.-
  N5: D3.cathode, R3.Pin_1, S1.Pin_3, S1.Pin_4, パーツ1.D3_PWM
  N6: R5.Pin_0, R6.wiper
  N7: R5.Pin_1, C1.1, パーツ1.A0

notes:
  GND
  +5V
  GateIn
  Delay
  Time
  Delayed Gate
