# Fritzing sketch Gate_In_Limitter_Test (saved by Fritzing 0.9.4)
breadboards: 1

parts:
  R2 = Resistor [tolerance=±5% resistance=4.7k package=THT]
  D1 = Rectifier Diode [part_number=1N4001 package="300 mil [THT]"]
  D2 = Rectifier Diode [part_number=1N4001 package="300 mil [THT]"]
  D3 = Rectifier Diode [part_number=1N4001 package="300 mil [THT]"]
  R3 = Resistor [tolerance=±5% resistance=100k package=THT]
  S1 = Pushbutton [package="[THT]"]
  R4 = Resistor [tolerance=±5% resistance=100k package=THT]

nets:
  N1: R2.Pin_0, R4.Pin_1
  N2: R2.Pin_1, D1.anode, D2.cathode, D3.anode
  N3: D1.cathode, S1.Pin_1, S1.Pin_2
  N4: D2.anode, R3.Pin_0, R4.Pin_0
  N5: D3.cathode, R3.Pin_1, S1.Pin_3, S1.Pin_4

notes:
  GND
  +5V
  GateIn
  Out
